# Fritzing sketch dht22_d1mini_solar (saved by Fritzing 0.9.4)

parts:
  WeMos_D1_Mini1 = WeMos D1 Mini
  DHT1 = DHT22 Humidity and Temperature Sensor
  D1 = Schottky Diode [part_number=1N5817 package="Melf DO-213 AB [SMD]"]
  R1 = Resistor [tolerance=±5% resistance=10k package=THT]
  Solar_Cell1 = 5V 100mA Polycrystalline PET Solar Cell [part_number=IM130407002]
  J1 = Generic female header - 2 pins [form="♀ (female)" package=THT]
  Part1 = TP4056 Charger
  R2 = Resistor [tolerance=±5% resistance=10k package=THT]

nets:
  3V3: WeMos_D1_Mini1.3V3, DHT1.VDD, R2.Pin_0
  N1: WeMos_D1_Mini1.5V, D1.cathode, R1.Pin_1, J1.+, Part1.IN+, Part1.BAT+
  N2: WeMos_D1_Mini1.A0, R1.Pin_0
  N3: WeMos_D1_Mini1.D0, WeMos_D1_Mini1.RST
  N4: WeMos_D1_Mini1.D2, DHT1.DATA, R2.Pin_1
  GND: WeMos_D1_Mini1.G, DHT1.GND, Solar_Cell1.GND, J1.-, Part1.IN-, Part1.BAT-

custom parts:
  5V 100mA Polycrystalline PET Solar Cell: This is 5V 100mA Polycrystalline PET Solar Cell. It is high quality and exquisite appearance. It is used in all kinds of high-grade electronic products.
  Generic female header - 2 pins: Generic female header
